// Logisim project C.MyAdder1b.circ as structural Verilog: 1 circuit, main circuit main
module main (
  input  P0,
  input  A,
  input  B,
  output S,
  output P
);

  wire and_1_out, and_2_out, xor_1_out;

  xor xor_1 (xor_1_out, A, B);
  and and_1 (and_1_out, A, B);
  xor xor_2 (S, P0, xor_1_out);
  and and_2 (and_2_out, xor_1_out, P0);
  or or_1 (P, and_2_out, and_1_out);

  // Notes on the sheet:
  //   FullAdder 1b Circuit
  //   Denis Bakushev
  //   Jun 14, 2023
endmodule
