// Logisim project G.BinaryShift.circ as structural Verilog: 2 circuits, main circuit main
module main (
  input  [7:0] in_1,
  input  in_2,
  input  [1:0] in_3,
  input  [2:0] in_4,
  output [7:0] out_5
);

  wire [7:0] bshift_1_out_4, bshift_2_out_4, bshift_3_out_4, bshift_4_out_4, bshift_5_out_4, bshift_6_out_4,
       bshift_7_out_4, bshift_8_out_4, demultiplexer_1_out0, demultiplexer_1_out1, demultiplexer_1_out2,
       demultiplexer_1_out3, demultiplexer_1_out4, demultiplexer_1_out5, demultiplexer_1_out6,
       demultiplexer_1_out7, xor_1_out, xor_2_out, xor_3_out, xor_4_out, xor_5_out, xor_6_out, xor_7_out;

  Demultiplexer #(.select(3), .width(8)) demultiplexer_1 (
    .out0(demultiplexer_1_out0), .out1(demultiplexer_1_out1), .out2(demultiplexer_1_out2),
    .out3(demultiplexer_1_out3), .out4(demultiplexer_1_out4), .out5(demultiplexer_1_out5),
    .out6(demultiplexer_1_out6), .out7(demultiplexer_1_out7), .in(in_1), .sel(in_4));
  BShift bshift_1 (.in_2(in_2), .in_3(in_3), .out_4(bshift_1_out_4));  // open: in_1
  BShift bshift_2 (.in_1(xor_1_out), .in_2(in_2), .in_3(in_3), .out_4(bshift_2_out_4));
  BShift bshift_3 (.in_1(xor_2_out), .in_2(in_2), .in_3(in_3), .out_4(bshift_3_out_4));
  BShift bshift_4 (.in_1(xor_3_out), .in_2(in_2), .in_3(in_3), .out_4(bshift_4_out_4));
  BShift bshift_5 (.in_1(xor_4_out), .in_2(in_2), .in_3(in_3), .out_4(bshift_5_out_4));
  BShift bshift_6 (.in_1(xor_5_out), .in_2(in_2), .in_3(in_3), .out_4(bshift_6_out_4));
  BShift bshift_7 (.in_1(xor_6_out), .in_2(in_2), .in_3(in_3), .out_4(bshift_7_out_4));
  BShift bshift_8 (.in_1(xor_7_out), .in_2(in_2), .in_3(in_3), .out_4(bshift_8_out_4));
  assign xor_1_out = bshift_1_out_4 ^ demultiplexer_1_out7;  // XOR_Gate xor_1, 8 bits wide
  assign xor_2_out = bshift_2_out_4 ^ demultiplexer_1_out6;  // XOR_Gate xor_2, 8 bits wide
  assign xor_3_out = bshift_3_out_4 ^ demultiplexer_1_out5;  // XOR_Gate xor_3, 8 bits wide
  assign xor_4_out = bshift_4_out_4 ^ demultiplexer_1_out4;  // XOR_Gate xor_4, 8 bits wide
  assign xor_5_out = bshift_5_out_4 ^ demultiplexer_1_out3;  // XOR_Gate xor_5, 8 bits wide
  assign xor_6_out = bshift_6_out_4 ^ demultiplexer_1_out2;  // XOR_Gate xor_6, 8 bits wide
  assign xor_7_out = bshift_7_out_4 ^ demultiplexer_1_out1;  // XOR_Gate xor_7, 8 bits wide
  assign out_5 = bshift_8_out_4 ^ demultiplexer_1_out0;  // XOR_Gate xor_8, 8 bits wide

  // Notes on the sheet:
  //   Binary Shift Circuit
  //   Denis Bakushev
  //   Jun 16, 2023
endmodule

module BShift (
  input  [7:0] in_1,
  input  in_2,
  input  [1:0] in_3,
  output [7:0] out_4
);

  wire and_1_out, and_2_out, and_3_out, and_4_out, and_5_out, and_6_out, and_7_out, and_8_out, and_9_out,
       and_10_out, and_11_out, and_12_out, and_13_out, and_14_out, and_15_out, and_16_out, and_17_out,
       and_18_out, and_19_out, not_1_out, or_1_out;

  not not_1 (not_1_out, in_2);
  and and_1 (and_1_out, in_2, in_1[0]);
  and and_2 (and_2_out, in_1[0], not_1_out);
  and and_3 (and_3_out, in_2, in_1[1]);
  and and_4 (and_4_out, in_1[1], not_1_out);
  and and_5 (and_5_out, in_2, in_1[2]);
  and and_6 (and_6_out, in_1[2], not_1_out);
  and and_7 (and_7_out, in_2, in_1[3]);
  and and_8 (and_8_out, in_1[3], not_1_out);
  and and_9 (and_9_out, in_2, in_1[4]);
  and and_10 (and_10_out, in_1[4], not_1_out);
  and and_11 (and_11_out, in_2, in_1[5]);
  and and_12 (and_12_out, in_1[5], not_1_out);
  and and_13 (and_13_out, in_2, in_1[6]);
  and and_14 (and_14_out, in_1[6], not_1_out);
  and and_15 (and_15_out, in_2, in_1[7]);
  and and_16 (and_16_out, in_1[7], not_1_out);
  and and_17 (and_17_out, in_3[0], and_15_out);
  and and_18 (and_18_out, in_3[1], and_1_out);
  and and_19 (and_19_out, in_3[1], and_16_out);
  or or_1 (or_1_out, and_17_out, and_18_out);
  or or_2 (out_4[0], and_19_out, and_3_out);
  or or_3 (out_4[1], and_2_out, and_5_out);
  or or_4 (out_4[2], and_4_out, and_7_out);
  or or_5 (out_4[3], and_6_out, and_9_out);
  or or_6 (out_4[4], and_8_out, and_11_out);
  or or_7 (out_4[5], and_10_out, and_13_out);
  or or_8 (out_4[6], and_12_out, and_15_out);
  or or_9 (out_4[7], and_14_out, or_1_out);
endmodule
