// Logisim project H.MyComparator.circ as structural Verilog: 2 circuits, main circuit main
module main (
  input  [7:0] in_1,
  input  [7:0] in_2,
  output A_B,
  output A__B,
  output A_B_2,
  output A__B_2,
  output A_B_3
);

  wire and_2_out, and_3_out, and_4_out, and_5_out, and_6_out, and_7_out, and_8_out, and_9_out, and_10_out,
       and_11_out, and_12_out, and_13_out, and_14_out, and_15_out, and_16_out, and_17_out, and_18_out,
       and_19_out, and_20_out, and_21_out, comparator1b_1_a_b, comparator1b_1_a_b_2, comparator1b_1_a_b_3,
       comparator1b_2_a_b, comparator1b_2_a_b_2, comparator1b_2_a_b_3, comparator1b_3_a_b,
       comparator1b_3_a_b_2, comparator1b_3_a_b_3, comparator1b_4_a_b, comparator1b_4_a_b_2,
       comparator1b_4_a_b_3, comparator1b_5_a_b, comparator1b_5_a_b_2, comparator1b_5_a_b_3,
       comparator1b_6_a_b, comparator1b_6_a_b_2, comparator1b_6_a_b_3, comparator1b_7_a_b,
       comparator1b_7_a_b_2, comparator1b_7_a_b_3, comparator1b_8_a_b, comparator1b_8_a_b_2,
       comparator1b_8_a_b_3;

  Comparator1b comparator1b_1 (
    .A(in_1[0]), .B(in_2[0]), .A_B(comparator1b_1_a_b), .A_B_2(comparator1b_1_a_b_2),
    .A_B_3(comparator1b_1_a_b_3));
  Comparator1b comparator1b_2 (
    .A(in_1[1]), .B(in_2[1]), .A_B(comparator1b_2_a_b), .A_B_2(comparator1b_2_a_b_2),
    .A_B_3(comparator1b_2_a_b_3));
  Comparator1b comparator1b_3 (
    .A(in_1[2]), .B(in_2[2]), .A_B(comparator1b_3_a_b), .A_B_2(comparator1b_3_a_b_2),
    .A_B_3(comparator1b_3_a_b_3));
  Comparator1b comparator1b_4 (
    .A(in_1[3]), .B(in_2[3]), .A_B(comparator1b_4_a_b), .A_B_2(comparator1b_4_a_b_2),
    .A_B_3(comparator1b_4_a_b_3));
  Comparator1b comparator1b_5 (
    .A(in_1[4]), .B(in_2[4]), .A_B(comparator1b_5_a_b), .A_B_2(comparator1b_5_a_b_2),
    .A_B_3(comparator1b_5_a_b_3));
  Comparator1b comparator1b_6 (
    .A(in_1[5]), .B(in_2[5]), .A_B(comparator1b_6_a_b), .A_B_2(comparator1b_6_a_b_2),
    .A_B_3(comparator1b_6_a_b_3));
  Comparator1b comparator1b_7 (
    .A(in_1[6]), .B(in_2[6]), .A_B(comparator1b_7_a_b), .A_B_2(comparator1b_7_a_b_2),
    .A_B_3(comparator1b_7_a_b_3));
  Comparator1b comparator1b_8 (
    .A(in_1[7]), .B(in_2[7]), .A_B(comparator1b_8_a_b), .A_B_2(comparator1b_8_a_b_2),
    .A_B_3(comparator1b_8_a_b_3));
  and and_1 (A_B_2, comparator1b_1_a_b_2, and_2_out);
  and and_2 (and_2_out, comparator1b_2_a_b_2, and_3_out);
  and and_3 (and_3_out, comparator1b_3_a_b_2, and_4_out);
  and and_4 (and_4_out, comparator1b_4_a_b_2, and_5_out);
  and and_5 (and_5_out, comparator1b_5_a_b_2, and_6_out);
  and and_6 (and_6_out, comparator1b_6_a_b_2, and_7_out);
  and and_7 (and_7_out, comparator1b_7_a_b_2, comparator1b_8_a_b_2);
  and and_8 (and_8_out, comparator1b_1_a_b_3, and_2_out);
  and and_9 (and_9_out, comparator1b_2_a_b_3, and_3_out);
  and and_10 (and_10_out, comparator1b_3_a_b_3, and_4_out);
  and and_11 (and_11_out, comparator1b_4_a_b_3, and_5_out);
  and and_12 (and_12_out, comparator1b_5_a_b_3, and_6_out);
  and and_13 (and_13_out, comparator1b_6_a_b_3, and_7_out);
  and and_14 (and_14_out, comparator1b_7_a_b_3, comparator1b_8_a_b_2);
  and and_15 (and_15_out, comparator1b_1_a_b, and_2_out);
  and and_16 (and_16_out, comparator1b_2_a_b, and_3_out);
  and and_17 (and_17_out, comparator1b_3_a_b, and_4_out);
  and and_18 (and_18_out, comparator1b_4_a_b, and_5_out);
  and and_19 (and_19_out, comparator1b_5_a_b, and_6_out);
  and and_20 (and_20_out, comparator1b_6_a_b, and_7_out);
  and and_21 (and_21_out, comparator1b_7_a_b, comparator1b_8_a_b_2);
  or or_1 (A_B, and_15_out, and_16_out, and_17_out, and_18_out, and_19_out, and_20_out, and_21_out, comparator1b_8_a_b_3);
  or or_2 (A_B_3, and_8_out, and_9_out, and_10_out, and_11_out, and_12_out, and_13_out, and_14_out, comparator1b_8_a_b);
  or or_3 (A__B, A_B, A_B_2);
  or or_4 (A__B_2, A_B_2, A_B_3);

  // Notes on the sheet:
  //   A
  //   B
  //   Comaparator 8b Signed Circuit
  //   Denis Bakushev
  //   Jun 17, 2023
endmodule

module Comparator1b (
  input  A,
  input  B,
  output A_B,
  output A_B_2,
  output A_B_3
);

  wire not_1_out, or_1_out, xor_1_out;

  and and_1 (A_B, A, not_1_out);
  not not_1 (not_1_out, B);
  xor xor_1 (xor_1_out, A, B);
  not not_2 (A_B_2, xor_1_out);
  or or_1 (or_1_out, A_B, A_B_2);
  not not_3 (A_B_3, or_1_out);
endmodule
