// Logisim project HalfAdder.circ as structural Verilog: 1 circuit, main circuit main
module main (
  input  A,
  input  B,
  output S,
  output P
);

  xor xor_1 (S, A, B);
  and and_1 (P, A, B);

  // Notes on the sheet:
  //   HalfAdder 1b Circuit
  //   Denis Bakushev
  //   Jun 14, 2023
endmodule
