// Logisim project I.Multiplier8bSigned.circ as structural Verilog: 2 circuits, main circuit main
module main (
  input  [7:0] in_1,
  input  [7:0] in_2,
  output [15:0] out_3
);

  wire xor_1_out;
  wire [7:0] adder_1_out, adder_2_out, multiplexer_1_out, multiplexer_2_out, not_1_out, not_2_out;
  wire [15:0] multiplier8bunsigned_1_out_3, not_3_out, subtractor_1_out;

  Adder adder_1 (.a(8'h1), .b(not_1_out), .out(adder_1_out));  // open: cin, cout
  assign not_1_out = ~in_1;  // NOT_Gate not_1, 8 bits wide
  Adder adder_2 (.a(8'h1), .b(not_2_out), .out(adder_2_out));  // open: cin, cout
  assign not_2_out = ~in_2;  // NOT_Gate not_2, 8 bits wide
  Multiplexer #(.width(8)) multiplexer_1 (.in0(in_1), .in1(adder_1_out), .out(multiplexer_1_out), .sel(in_1[7]));
  Multiplexer #(.width(8)) multiplexer_2 (.in0(in_2), .in1(adder_2_out), .out(multiplexer_2_out), .sel(in_2[7]));
  Multiplier8bUnsigned multiplier8bunsigned_1 (
    .in_1(multiplexer_1_out), .in_2(multiplexer_2_out), .out_3(multiplier8bunsigned_1_out_3));
  xor xor_1 (xor_1_out, in_1[7], in_2[7]);
  Subtractor #(.width(16)) subtractor_1 (
    .a(multiplier8bunsigned_1_out_3), .b(16'h1), .out(subtractor_1_out));  // open: bin, bout
  Multiplexer #(.width(16)) multiplexer_3 (
    .in0(multiplier8bunsigned_1_out_3), .in1(not_3_out), .out(out_3), .sel(xor_1_out));
  assign not_3_out = ~subtractor_1_out;  // NOT_Gate not_3, 16 bits wide

  // Notes on the sheet:
  //   A
  //   B
  //   Multiplier 8b Signed Circuit
  //   Denis Bakushev
  //   Jun 17, 2023
  //   C
endmodule

module Multiplier8bUnsigned (
  input  [7:0] in_1,
  input  [7:0] in_2,
  output [15:0] out_3
);

  wire [15:0] adder_1_out, adder_2_out, adder_3_out, adder_4_out, adder_5_out, adder_6_out, and_1_out,
       and_2_out, and_3_out, and_4_out, and_5_out, and_6_out, and_7_out, and_8_out, bit_extender_1_out,
       bit_extender_2_out, bit_extender_3_out, bit_extender_4_out, bit_extender_5_out, bit_extender_6_out,
       bit_extender_7_out, bit_extender_8_out, bit_extender_9_out, shifter_1_out, shifter_2_out,
       shifter_3_out, shifter_4_out, shifter_5_out, shifter_6_out, shifter_7_out;

  assign bit_extender_1_out = {{8{in_1[7]}}, in_1};  // Bit_Extender bit_extender_1
  assign bit_extender_2_out = {{15{in_2[0]}}, in_2[0]};  // Bit_Extender bit_extender_2
  assign bit_extender_3_out = {{15{in_2[1]}}, in_2[1]};  // Bit_Extender bit_extender_3
  assign bit_extender_4_out = {{15{in_2[2]}}, in_2[2]};  // Bit_Extender bit_extender_4
  assign bit_extender_5_out = {{15{in_2[3]}}, in_2[3]};  // Bit_Extender bit_extender_5
  assign bit_extender_6_out = {{15{in_2[4]}}, in_2[4]};  // Bit_Extender bit_extender_6
  assign bit_extender_7_out = {{15{in_2[5]}}, in_2[5]};  // Bit_Extender bit_extender_7
  assign bit_extender_8_out = {{15{in_2[6]}}, in_2[6]};  // Bit_Extender bit_extender_8
  assign bit_extender_9_out = {{15{in_2[7]}}, in_2[7]};  // Bit_Extender bit_extender_9
  Shifter #(.width(16)) shifter_1 (.in(bit_extender_1_out), .\dist (4'b0001), .out(shifter_1_out));
  Shifter #(.width(16)) shifter_2 (.in(bit_extender_1_out), .\dist (4'b0010), .out(shifter_2_out));
  Shifter #(.width(16)) shifter_3 (.in(bit_extender_1_out), .\dist (4'b0011), .out(shifter_3_out));
  Shifter #(.width(16)) shifter_4 (.in(bit_extender_1_out), .\dist (4'b0100), .out(shifter_4_out));
  Shifter #(.width(16)) shifter_5 (.in(bit_extender_1_out), .\dist (4'b0101), .out(shifter_5_out));
  Shifter #(.width(16)) shifter_6 (.in(bit_extender_1_out), .\dist (4'b0110), .out(shifter_6_out));
  Shifter #(.width(16)) shifter_7 (.in(bit_extender_1_out), .\dist (4'b0111), .out(shifter_7_out));
  assign and_1_out = bit_extender_1_out & bit_extender_2_out;  // AND_Gate and_1, 16 bits wide
  assign and_2_out = shifter_1_out & bit_extender_3_out;  // AND_Gate and_2, 16 bits wide
  assign and_3_out = shifter_2_out & bit_extender_4_out;  // AND_Gate and_3, 16 bits wide
  assign and_4_out = shifter_3_out & bit_extender_5_out;  // AND_Gate and_4, 16 bits wide
  assign and_5_out = shifter_4_out & bit_extender_6_out;  // AND_Gate and_5, 16 bits wide
  assign and_6_out = shifter_5_out & bit_extender_7_out;  // AND_Gate and_6, 16 bits wide
  assign and_7_out = shifter_6_out & bit_extender_8_out;  // AND_Gate and_7, 16 bits wide
  assign and_8_out = shifter_7_out & bit_extender_9_out;  // AND_Gate and_8, 16 bits wide
  Adder #(.width(16)) adder_1 (.a(and_1_out), .b(and_2_out), .out(adder_1_out));  // open: cin, cout
  Adder #(.width(16)) adder_2 (.a(adder_1_out), .b(and_3_out), .out(adder_2_out));  // open: cin, cout
  Adder #(.width(16)) adder_3 (.a(adder_2_out), .b(and_4_out), .out(adder_3_out));  // open: cin, cout
  Adder #(.width(16)) adder_4 (.a(adder_3_out), .b(and_5_out), .out(adder_4_out));  // open: cin, cout
  Adder #(.width(16)) adder_5 (.a(adder_4_out), .b(and_6_out), .out(adder_5_out));  // open: cin, cout
  Adder #(.width(16)) adder_6 (.a(adder_5_out), .b(and_7_out), .out(adder_6_out));  // open: cin, cout
  Adder #(.width(16)) adder_7 (.a(adder_6_out), .b(and_8_out), .out(out_3));  // open: cin, cout

  // Notes on the sheet:
  //   A
  //   B
  //   C
endmodule
