// Logisim project K.L.Divider8bSigned.circ as structural Verilog: 3 circuits, main circuit main
module main (
  input  [7:0] in_1,
  input  [7:0] in_2,
  output [7:0] out_3,
  output [7:0] out_4
);

  wire xor_1_out;
  wire [7:0] adder_1_out, adder_2_out, divider8bunsigned_1_out_3, divider8bunsigned_1_out_4,
       multiplexer_1_out, multiplexer_2_out, not_1_out, not_2_out, not_3_out, not_4_out, subtractor_1_out,
       subtractor_2_out;

  assign not_1_out = ~in_1;  // NOT_Gate not_1, 8 bits wide
  assign not_2_out = ~in_2;  // NOT_Gate not_2, 8 bits wide
  xor xor_1 (xor_1_out, in_1[7], in_2[7]);
  Multiplexer #(.width(8)) multiplexer_1 (.in0(in_1), .in1(adder_1_out), .out(multiplexer_1_out), .sel(in_1[7]));
  Adder adder_1 (.a(not_1_out), .b(8'h1), .out(adder_1_out));  // open: cin, cout
  Multiplexer #(.width(8)) multiplexer_2 (.in0(in_2), .in1(adder_2_out), .out(multiplexer_2_out), .sel(in_2[7]));
  Adder adder_2 (.a(not_2_out), .b(8'h1), .out(adder_2_out));  // open: cin, cout
  Divider8bUnsigned divider8bunsigned_1 (
    .in_1(multiplexer_1_out), .in_2(multiplexer_2_out), .out_3(divider8bunsigned_1_out_3),
    .out_4(divider8bunsigned_1_out_4));
  Subtractor subtractor_1 (.a(divider8bunsigned_1_out_3), .b(8'h1), .out(subtractor_1_out));  // open: bin, bout
  assign not_3_out = ~subtractor_2_out;  // NOT_Gate not_3, 8 bits wide
  Subtractor subtractor_2 (.a(divider8bunsigned_1_out_4), .b(8'h1), .out(subtractor_2_out));  // open: bin, bout
  Multiplexer #(.width(8)) multiplexer_3 (
    .in0(divider8bunsigned_1_out_3), .in1(not_4_out), .out(out_3), .sel(xor_1_out));
  assign not_4_out = ~subtractor_1_out;  // NOT_Gate not_4, 8 bits wide
  Multiplexer #(.width(8)) multiplexer_4 (.in0(divider8bunsigned_1_out_4), .in1(not_3_out), .out(out_4), .sel(in_1[7]));

  // Notes on the sheet:
  //   A
  //   B
  //   Divider 8b Signed Circuit
  //   Denis Bakushev
  //   Jun 22, 2023
  //   C
  //   D
endmodule

module Divider8bUnsigned (
  input  [7:0] in_1,
  input  [7:0] in_2,
  output [7:0] out_3,
  output [7:0] out_4
);

  wire comparator_1_eq, comparator_2_eq, comparator_3_gt, comparator_4_lt, comparator_5_lt, comparator_6_lt,
       comparator_7_lt, comparator_8_lt, comparator_9_lt, comparator_10_lt, comparator_11_lt,
       comparator_12_eq, comparator_13_eq, comparator_14_eq, comparator_15_eq, comparator_16_eq,
       comparator_17_eq, comparator_18_eq, comparator_19_eq, demultiplexer_2_out1, demultiplexer_2_out2,
       demultiplexer_2_out3, demultiplexer_2_out4, demultiplexer_2_out5, demultiplexer_2_out6,
       demultiplexer_2_out7, or_9_out, or_10_out, or_11_out, or_12_out, or_13_out, or_14_out, or_15_out,
       or_16_out, or_17_out, or_18_out, or_19_out, or_20_out, or_21_out, or_22_out, or_23_out, or_24_out;
  wire [2:0] bitfinder_1_index;
  wire [7:0] demultiplexer_1_out0, demultiplexer_1_out1, demultiplexer_1_out2, demultiplexer_1_out3,
       demultiplexer_1_out4, demultiplexer_1_out5, demultiplexer_1_out6, demultiplexer_1_out7,
       multiplexer_1_out, multiplexer_2_out, multiplexer_3_out, multiplexer_4_out, multiplexer_5_out,
       multiplexer_6_out, multiplexer_7_out, multiplier_1_out, mysubtractor_1_out_3, mysubtractor_2_out_3,
       mysubtractor_3_out_3, mysubtractor_4_out_3, mysubtractor_5_out_3, mysubtractor_6_out_3,
       mysubtractor_7_out_3, mysubtractor_8_out_3, not_8_out, or_1_out, or_2_out, or_3_out, or_4_out,
       or_5_out, or_6_out, or_7_out, or_8_out, shifter_1_out, shifter_2_out, shifter_3_out, shifter_4_out,
       shifter_5_out, shifter_6_out, shifter_7_out;

  Demultiplexer #(.select(3), .width(8)) demultiplexer_1 (
    .out0(demultiplexer_1_out0), .out1(demultiplexer_1_out1), .out2(demultiplexer_1_out2),
    .out3(demultiplexer_1_out3), .out4(demultiplexer_1_out4), .out5(demultiplexer_1_out5),
    .out6(demultiplexer_1_out6), .out7(demultiplexer_1_out7), .in(in_1), .sel(bitfinder_1_index));
  BitFinder #(.\type ("high1")) bitfinder_1 (.in(in_2), .index(bitfinder_1_index));  // open: found
  assign or_1_out = {8{1'b0}} | demultiplexer_1_out0;  // OR_Gate or_1, 8 bits wide
  assign or_2_out = or_1_out | demultiplexer_1_out1;  // OR_Gate or_2, 8 bits wide
  assign or_3_out = multiplexer_1_out | demultiplexer_1_out2;  // OR_Gate or_3, 8 bits wide
  assign or_4_out = multiplexer_2_out | demultiplexer_1_out3;  // OR_Gate or_4, 8 bits wide
  assign or_5_out = multiplexer_3_out | demultiplexer_1_out4;  // OR_Gate or_5, 8 bits wide
  assign or_6_out = multiplexer_4_out | demultiplexer_1_out5;  // OR_Gate or_6, 8 bits wide
  assign or_7_out = multiplexer_5_out | demultiplexer_1_out6;  // OR_Gate or_7, 8 bits wide
  assign or_8_out = multiplexer_6_out | demultiplexer_1_out7;  // OR_Gate or_8, 8 bits wide
  Shifter shifter_1 (.in(in_2), .\dist (3'b111), .out(shifter_1_out));
  Shifter shifter_2 (.in(in_2), .\dist (3'b110), .out(shifter_2_out));
  Shifter shifter_3 (.in(in_2), .\dist (3'b101), .out(shifter_3_out));
  Shifter shifter_4 (.in(in_2), .\dist (3'b100), .out(shifter_4_out));
  Shifter shifter_5 (.in(in_2), .\dist (3'b011), .out(shifter_5_out));
  Shifter shifter_6 (.in(in_2), .\dist (3'b010), .out(shifter_6_out));
  Shifter shifter_7 (.in(in_2), .\dist (3'b001), .out(shifter_7_out));
  Comparator comparator_1 (.a(in_2), .b({8{1'b0}}), .eq(comparator_1_eq));  // open: gt, lt
  Comparator comparator_2 (.a(in_1), .b({8{1'b0}}), .eq(comparator_2_eq));  // open: gt, lt
  Comparator #(.mode("unsigned")) comparator_3 (.a(in_2), .b(in_1), .gt(comparator_3_gt));  // open: eq, lt
  Multiplexer #(.width(8)) multiplexer_1 (
    .in0(mysubtractor_1_out_3), .in1(or_2_out), .out(multiplexer_1_out), .sel(or_10_out));
  Multiplexer #(.width(8)) multiplexer_2 (
    .in0(mysubtractor_2_out_3), .in1(or_3_out), .out(multiplexer_2_out), .sel(or_11_out));
  Multiplexer #(.width(8)) multiplexer_3 (
    .in0(mysubtractor_3_out_3), .in1(or_4_out), .out(multiplexer_3_out), .sel(or_12_out));
  Multiplexer #(.width(8)) multiplexer_4 (
    .in0(mysubtractor_4_out_3), .in1(or_5_out), .out(multiplexer_4_out), .sel(or_13_out));
  Multiplexer #(.width(8)) multiplexer_5 (
    .in0(mysubtractor_5_out_3), .in1(or_6_out), .out(multiplexer_5_out), .sel(or_14_out));
  Multiplexer #(.width(8)) multiplexer_6 (
    .in0(mysubtractor_6_out_3), .in1(or_7_out), .out(multiplexer_6_out), .sel(or_15_out));
  Multiplexer #(.width(8)) multiplexer_7 (
    .in0(mysubtractor_7_out_3), .in1(or_8_out), .out(multiplexer_7_out), .sel(or_16_out));
  or or_9 (or_9_out, comparator_1_eq, comparator_2_eq, comparator_3_gt);
  MySubtractor mysubtractor_1 (.in_1(or_1_out), .in_2(shifter_1_out), .out_3(mysubtractor_1_out_3));
  MySubtractor mysubtractor_2 (.in_1(multiplexer_1_out), .in_2(shifter_2_out), .out_3(mysubtractor_2_out_3));
  MySubtractor mysubtractor_3 (.in_1(multiplexer_2_out), .in_2(shifter_3_out), .out_3(mysubtractor_3_out_3));
  MySubtractor mysubtractor_4 (.in_1(multiplexer_3_out), .in_2(shifter_4_out), .out_3(mysubtractor_4_out_3));
  MySubtractor mysubtractor_5 (.in_1(multiplexer_4_out), .in_2(shifter_5_out), .out_3(mysubtractor_5_out_3));
  MySubtractor mysubtractor_6 (.in_1(multiplexer_5_out), .in_2(shifter_6_out), .out_3(mysubtractor_6_out_3));
  MySubtractor mysubtractor_7 (.in_1(multiplexer_6_out), .in_2(shifter_7_out), .out_3(mysubtractor_7_out_3));
  MySubtractor mysubtractor_8 (.in_1(multiplexer_7_out), .in_2(in_2), .out_3(mysubtractor_8_out_3));
  Comparator comparator_4 (.a(mysubtractor_1_out_3), .b({8{1'b0}}), .lt(comparator_4_lt));  // open: gt, eq
  or or_10 (or_10_out, demultiplexer_2_out1, comparator_4_lt);
  Comparator comparator_5 (.a(mysubtractor_2_out_3), .b({8{1'b0}}), .lt(comparator_5_lt));  // open: gt, eq
  or or_11 (or_11_out, demultiplexer_2_out2, comparator_5_lt);
  Comparator comparator_6 (.a(mysubtractor_3_out_3), .b({8{1'b0}}), .lt(comparator_6_lt));  // open: gt, eq
  or or_12 (or_12_out, demultiplexer_2_out3, comparator_6_lt);
  Comparator comparator_7 (.a(mysubtractor_4_out_3), .b({8{1'b0}}), .lt(comparator_7_lt));  // open: gt, eq
  or or_13 (or_13_out, demultiplexer_2_out4, comparator_7_lt);
  Comparator comparator_8 (.a(mysubtractor_5_out_3), .b({8{1'b0}}), .lt(comparator_8_lt));  // open: gt, eq
  or or_14 (or_14_out, demultiplexer_2_out5, comparator_8_lt);
  Comparator comparator_9 (.a(mysubtractor_6_out_3), .b({8{1'b0}}), .lt(comparator_9_lt));  // open: gt, eq
  or or_15 (or_15_out, demultiplexer_2_out6, comparator_9_lt);
  Comparator comparator_10 (.a(mysubtractor_7_out_3), .b({8{1'b0}}), .lt(comparator_10_lt));  // open: gt, eq
  or or_16 (or_16_out, demultiplexer_2_out7, comparator_10_lt);
  Comparator comparator_11 (.a(mysubtractor_8_out_3), .b({8{1'b0}}), .lt(comparator_11_lt));  // open: gt, eq
  Demultiplexer #(.select(3)) demultiplexer_2 (
    .out1(demultiplexer_2_out1), .out2(demultiplexer_2_out2), .out3(demultiplexer_2_out3),
    .out4(demultiplexer_2_out4), .out5(demultiplexer_2_out5), .out6(demultiplexer_2_out6),
    .out7(demultiplexer_2_out7), .in(1'b1), .sel(bitfinder_1_index));  // open: out0
  Comparator comparator_12 (.a(or_1_out), .b({8{1'b0}}), .eq(comparator_12_eq));  // open: gt, lt
  Comparator comparator_13 (.a(multiplexer_1_out), .b({8{1'b0}}), .eq(comparator_13_eq));  // open: gt, lt
  Comparator comparator_14 (.a(multiplexer_2_out), .b({8{1'b0}}), .eq(comparator_14_eq));  // open: gt, lt
  Comparator comparator_15 (.a(multiplexer_3_out), .b({8{1'b0}}), .eq(comparator_15_eq));  // open: gt, lt
  Comparator comparator_16 (.a(multiplexer_4_out), .b({8{1'b0}}), .eq(comparator_16_eq));  // open: gt, lt
  Comparator comparator_17 (.a(multiplexer_5_out), .b({8{1'b0}}), .eq(comparator_17_eq));  // open: gt, lt
  Comparator comparator_18 (.a(multiplexer_6_out), .b({8{1'b0}}), .eq(comparator_18_eq));  // open: gt, lt
  Comparator comparator_19 (.a(multiplexer_7_out), .b({8{1'b0}}), .eq(comparator_19_eq));  // open: gt, lt
  Multiplier multiplier_1 (.a(out_3), .b(in_2), .out(multiplier_1_out));  // open: cin, cout
  or or_17 (or_17_out, comparator_4_lt, comparator_12_eq);
  not not_1 (not_8_out[7], or_17_out);
  or or_18 (or_18_out, comparator_5_lt, comparator_13_eq);
  not not_2 (not_8_out[6], or_18_out);
  or or_19 (or_19_out, comparator_6_lt, comparator_14_eq);
  not not_3 (not_8_out[5], or_19_out);
  or or_20 (or_20_out, comparator_7_lt, comparator_15_eq);
  not not_4 (not_8_out[4], or_20_out);
  or or_21 (or_21_out, comparator_8_lt, comparator_16_eq);
  not not_5 (not_8_out[3], or_21_out);
  or or_22 (or_22_out, comparator_9_lt, comparator_17_eq);
  not not_6 (not_8_out[2], or_22_out);
  or or_23 (or_23_out, comparator_10_lt, comparator_18_eq);
  not not_7 (not_8_out[1], or_23_out);
  or or_24 (or_24_out, comparator_11_lt, comparator_19_eq);
  not not_8 (not_8_out[0], or_24_out);
  Subtractor subtractor_1 (.a(in_1), .b(multiplier_1_out), .out(out_4));  // open: bin, bout
  Multiplexer #(.width(8)) multiplexer_8 (.in0(not_8_out), .in1({8{1'b0}}), .out(out_3), .sel(or_9_out));
endmodule

module MySubtractor (
  input  [7:0] in_1,
  input  [7:0] in_2,
  output [7:0] out_3
);

  wire comparator_1_lt;
  wire [7:0] bit_extender_3_out;
  wire [8:0] bit_extender_1_out, bit_extender_2_out, subtractor_1_out;

  assign bit_extender_1_out = {{1{1'b0}}, in_1};  // Bit_Extender bit_extender_1
  Subtractor #(.width(9)) subtractor_1 (
    .a(bit_extender_1_out), .b(bit_extender_2_out), .out(subtractor_1_out));  // open: bin, bout
  assign bit_extender_2_out = {{1{1'b0}}, in_2};  // Bit_Extender bit_extender_2
  Comparator #(.width(9)) comparator_1 (.a(subtractor_1_out), .b({9{1'b0}}), .lt(comparator_1_lt));  // open: gt, eq
  Bit_Extender #(.in_width(9), .out_width(8)) bit_extender_3 (.in(subtractor_1_out), .out(bit_extender_3_out));
  Multiplexer #(.width(8)) multiplexer_1 (.in0(bit_extender_3_out), .in1(8'h80), .out(out_3), .sel(comparator_1_lt));
endmodule
