// Logisim project MyAdder8b.circ as structural Verilog: 2 circuits, main circuit main
module main (
  input  [7:0] in_1,
  input  [7:0] in_2,
  output [7:0] out_3
);

  wire myadder1b_1_p, myadder1b_2_p, myadder1b_3_p, myadder1b_4_p, myadder1b_5_p, myadder1b_6_p,
       myadder1b_7_p;

  MyAdder1b myadder1b_1 (.in_1(1'b0), .in_2(in_1[0]), .in_3(in_2[0]), .S(out_3[0]), .P(myadder1b_1_p));
  MyAdder1b myadder1b_2 (.in_1(myadder1b_1_p), .in_2(in_1[1]), .in_3(in_2[1]), .S(out_3[1]), .P(myadder1b_2_p));
  MyAdder1b myadder1b_3 (.in_1(myadder1b_2_p), .in_2(in_1[2]), .in_3(in_2[2]), .S(out_3[2]), .P(myadder1b_3_p));
  MyAdder1b myadder1b_4 (.in_1(myadder1b_3_p), .in_2(in_1[3]), .in_3(in_2[3]), .S(out_3[3]), .P(myadder1b_4_p));
  MyAdder1b myadder1b_5 (.in_1(myadder1b_4_p), .in_2(in_1[4]), .in_3(in_2[4]), .S(out_3[4]), .P(myadder1b_5_p));
  MyAdder1b myadder1b_6 (.in_1(myadder1b_5_p), .in_2(in_1[5]), .in_3(in_2[5]), .S(out_3[5]), .P(myadder1b_6_p));
  MyAdder1b myadder1b_7 (.in_1(myadder1b_6_p), .in_2(in_1[6]), .in_3(in_2[6]), .S(out_3[6]), .P(myadder1b_7_p));
  MyAdder1b myadder1b_8 (.in_1(myadder1b_7_p), .in_2(in_1[7]), .in_3(in_2[7]), .S(out_3[7]));  // open: P

  // Notes on the sheet:
  //   FullAdder 8b Circuit
  //   Denis Bakushev
  //   Jun 15, 2023
endmodule

module MyAdder1b (
  input  in_1,
  input  in_2,
  input  in_3,
  output S,
  output P
);

  wire and_1_out, and_2_out, xor_1_out;

  xor xor_1 (xor_1_out, in_2, in_3);
  and and_1 (and_1_out, in_2, in_3);
  xor xor_2 (S, in_1, xor_1_out);
  and and_2 (and_2_out, xor_1_out, in_1);
  or or_1 (P, and_2_out, and_1_out);

  // Notes on the sheet:
  //   FullAdder 1b Circuit
  //   Denis Bakushev
  //   Jun 14, 2023
endmodule
