// Logisim project MyMultiplexer.circ as structural Verilog: 1 circuit, main circuit main
module main (
  input  [3:0] in_1,
  input  [3:0] in_2,
  input  [3:0] in_3,
  input  [3:0] in_4,
  input  [3:0] in_5,
  input  [3:0] in_6,
  input  [3:0] in_7,
  input  [3:0] in_8,
  input  [2:0] S,
  output [3:0] out_10
);

  wire not_1_out, not_2_out, not_3_out;
  wire [3:0] and_1_out, and_2_out, and_3_out, and_4_out, and_5_out, and_6_out, and_7_out, and_8_out,
       bit_extender_1_out, bit_extender_2_out, bit_extender_3_out, bit_extender_4_out, bit_extender_5_out,
       bit_extender_6_out;

  assign bit_extender_1_out = {{3{S[2]}}, S[2]};  // Bit_Extender bit_extender_1
  assign bit_extender_2_out = {{3{S[1]}}, S[1]};  // Bit_Extender bit_extender_2
  assign bit_extender_3_out = {{3{S[0]}}, S[0]};  // Bit_Extender bit_extender_3
  not not_1 (not_1_out, S[0]);
  not not_2 (not_2_out, S[1]);
  not not_3 (not_3_out, S[2]);
  assign bit_extender_4_out = {{3{not_3_out}}, not_3_out};  // Bit_Extender bit_extender_4
  assign bit_extender_5_out = {{3{not_2_out}}, not_2_out};  // Bit_Extender bit_extender_5
  assign bit_extender_6_out = {{3{not_1_out}}, not_1_out};  // Bit_Extender bit_extender_6
  assign and_1_out = in_1 & bit_extender_4_out & bit_extender_5_out & bit_extender_6_out;  // AND_Gate and_1, 4 bits wide
  assign and_2_out = in_2 & bit_extender_4_out & bit_extender_5_out & bit_extender_3_out;  // AND_Gate and_2, 4 bits wide
  assign and_3_out = in_3 & bit_extender_4_out & bit_extender_2_out & bit_extender_6_out;  // AND_Gate and_3, 4 bits wide
  assign and_4_out = in_4 & bit_extender_4_out & bit_extender_2_out & bit_extender_3_out;  // AND_Gate and_4, 4 bits wide
  assign and_5_out = in_5 & bit_extender_1_out & bit_extender_5_out & bit_extender_6_out;  // AND_Gate and_5, 4 bits wide
  assign and_6_out = in_6 & bit_extender_1_out & bit_extender_5_out & bit_extender_3_out;  // AND_Gate and_6, 4 bits wide
  assign and_7_out = in_7 & bit_extender_1_out & bit_extender_2_out & bit_extender_6_out;  // AND_Gate and_7, 4 bits wide
  assign and_8_out = in_8 & bit_extender_1_out & bit_extender_2_out & bit_extender_3_out;  // AND_Gate and_8, 4 bits wide
  assign out_10 = and_1_out | and_2_out | and_3_out | and_4_out | and_5_out | and_6_out | and_7_out | and_8_out;  // OR_Gate or_1, 4 bits wide

  // Notes on the sheet:
  //   A0
  //   A1
  //   A2
  //   A3
  //   A4
  //   A5
  //   A6
  //   A7
  //   Multiplexer Curcuit
  //   Denis Bakushev
  //   Jun 15, 2023
  //   B
endmodule
