// Logisim project Subtractor8b.circ as structural Verilog: 3 circuits, main circuit main
module main (
  input  [7:0] in_1,
  input  [7:0] in_2,
  output [7:0] out_3
);

  wire [7:0] fulladder8b_1_out_3, not_1_out;

  assign not_1_out = ~in_2;  // NOT_Gate not_1, 8 bits wide
  FullAdder8b fulladder8b_1 (.in_1(8'h1), .in_2(not_1_out), .out_3(fulladder8b_1_out_3));
  FullAdder8b fulladder8b_2 (.in_1(in_1), .in_2(fulladder8b_1_out_3), .out_3(out_3));

  // Notes on the sheet:
  //   Subtractor Circuit
  //   Denis Bakushev
  //   Jun 16, 2023
endmodule

module FullAdder8b (
  input  [7:0] in_1,
  input  [7:0] in_2,
  output [7:0] out_3
);

  wire fulladder1b_1_p, fulladder1b_2_p, fulladder1b_3_p, fulladder1b_4_p, fulladder1b_5_p, fulladder1b_6_p,
       fulladder1b_7_p;

  FullAdder1b fulladder1b_1 (.P0(1'b0), .A(in_1[0]), .B(in_2[0]), .S(out_3[0]), .P(fulladder1b_1_p));
  FullAdder1b fulladder1b_2 (.P0(fulladder1b_1_p), .A(in_1[1]), .B(in_2[1]), .S(out_3[1]), .P(fulladder1b_2_p));
  FullAdder1b fulladder1b_3 (.P0(fulladder1b_2_p), .A(in_1[2]), .B(in_2[2]), .S(out_3[2]), .P(fulladder1b_3_p));
  FullAdder1b fulladder1b_4 (.P0(fulladder1b_3_p), .A(in_1[3]), .B(in_2[3]), .S(out_3[3]), .P(fulladder1b_4_p));
  FullAdder1b fulladder1b_5 (.P0(fulladder1b_4_p), .A(in_1[4]), .B(in_2[4]), .S(out_3[4]), .P(fulladder1b_5_p));
  FullAdder1b fulladder1b_6 (.P0(fulladder1b_5_p), .A(in_1[5]), .B(in_2[5]), .S(out_3[5]), .P(fulladder1b_6_p));
  FullAdder1b fulladder1b_7 (.P0(fulladder1b_6_p), .A(in_1[6]), .B(in_2[6]), .S(out_3[6]), .P(fulladder1b_7_p));
  FullAdder1b fulladder1b_8 (.P0(fulladder1b_7_p), .A(in_1[7]), .B(in_2[7]), .S(out_3[7]));  // open: P

  // Notes on the sheet:
  //   FullAdder 8b Circuit
  //   Denis Bakushev
  //   Jun 15, 2023
endmodule

module FullAdder1b (
  input  P0,
  input  A,
  input  B,
  output S,
  output P
);

  wire and_1_out, and_2_out, xor_1_out;

  xor xor_1 (xor_1_out, A, B);
  and and_1 (and_1_out, A, B);
  xor xor_2 (S, P0, xor_1_out);
  and and_2 (and_2_out, xor_1_out, P0);
  or or_1 (P, and_2_out, and_1_out);

  // Notes on the sheet:
  //   FullAdder 1b Circuit
  //   Denis Bakushev
  //   Jun 14, 2023
endmodule
